# Fritzing sketch SmartGardenSchematic (saved by Fritzing 0.9.3b)
breadboards: 1

parts:
  Part1 = Arduino MKR1000
  R1 = PHOTOCELL [package=photocell-kit]
  R2 = Resistor [tolerance=±5% resistance=220 package=THT]
  U1 = TMP36 [package=to-92-kit]
  Part2 = Soil Moisture Sensor  # not connected

nets:
  N1: Part1.A1, U1.VOUT
  N2: Part1.A2, R1.P$2, R2.Pin_0
  GND: Part1.GND, R2.Pin_1, U1.GND
  VCC: Part1.VCC, R1.P$1, U1.VCC

custom parts:
  Arduino MKR1000: MKR1000 is a powerful board that combines the functionality of the Zero and the Wi-Fi Shield. It is the ideal solution for makers wanting to design IoT projects with minimal previous experience in networking
